// Digital circuit deslocador_direita.dig as structural Verilog
module deslocador_direita (
  input  [15:0] A,
  input  [15:0] B,
  output [15:0] Y
);

  wire mux8_1_1bit_1_y, mux8_1_1bit_2_y, mux8_1_1bit_3_y, mux8_1_1bit_4_y, mux8_1_1bit_5_y, mux8_1_1bit_6_y,
       mux8_1_1bit_7_y, mux8_1_1bit_8_y, mux8_1_1bit_9_y, mux8_1_1bit_10_y, mux8_1_1bit_11_y,
       mux8_1_1bit_12_y, mux8_1_1bit_13_y, mux8_1_1bit_14_y, mux8_1_1bit_15_y, mux8_1_1bit_16_y,
       mux8_1_1bit_17_y, mux8_1_1bit_18_y, mux8_1_1bit_19_y, mux8_1_1bit_20_y, mux8_1_1bit_21_y,
       mux8_1_1bit_22_y, mux8_1_1bit_23_y, mux8_1_1bit_24_y, mux8_1_1bit_25_y, mux8_1_1bit_26_y,
       mux8_1_1bit_27_y, mux8_1_1bit_28_y, mux8_1_1bit_29_y, mux8_1_1bit_30_y, mux8_1_1bit_31_y,
       mux8_1_1bit_32_y;

  mux8_1_1bit mux8_1_1bit_1 (
    .S(B[2:0]), .D_0(A[15]), .D_1(1'b0), .D_2(1'b0), .D_3(1'b0), .D_4(1'b0), .D_5(1'b0), .D_6(1'b0),
    .D_7(1'b0), .Y(mux8_1_1bit_1_y));
  mux8_1_1bit mux8_1_1bit_2 (
    .S(B[2:0]), .D_0(1'b0), .D_1(1'b0), .D_2(1'b0), .D_3(1'b0), .D_4(1'b0), .D_5(1'b0), .D_6(1'b0),
    .D_7(1'b0), .Y(mux8_1_1bit_2_y));
  mux8_1_1bit mux8_1_1bit_3 (
    .S(B[2:0]), .D_0(A[14]), .D_1(A[15]), .D_2(1'b0), .D_3(1'b0), .D_4(1'b0), .D_5(1'b0), .D_6(1'b0),
    .D_7(1'b0), .Y(mux8_1_1bit_3_y));
  mux8_1_1bit mux8_1_1bit_4 (
    .S(B[2:0]), .D_0(1'b0), .D_1(1'b0), .D_2(1'b0), .D_3(1'b0), .D_4(1'b0), .D_5(1'b0), .D_6(1'b0),
    .D_7(1'b0), .Y(mux8_1_1bit_4_y));
  mux8_1_1bit mux8_1_1bit_5 (
    .S(B[2:0]), .D_0(A[13]), .D_1(A[14]), .D_2(A[15]), .D_3(1'b0), .D_4(1'b0), .D_5(1'b0), .D_6(1'b0),
    .D_7(1'b0), .Y(mux8_1_1bit_5_y));
  mux8_1_1bit mux8_1_1bit_6 (
    .S(B[2:0]), .D_0(1'b0), .D_1(1'b0), .D_2(1'b0), .D_3(1'b0), .D_4(1'b0), .D_5(1'b0), .D_6(1'b0),
    .D_7(1'b0), .Y(mux8_1_1bit_6_y));
  mux8_1_1bit mux8_1_1bit_7 (
    .S(B[2:0]), .D_0(A[12]), .D_1(A[13]), .D_2(A[14]), .D_3(A[15]), .D_4(1'b0), .D_5(1'b0), .D_6(1'b0),
    .D_7(1'b0), .Y(mux8_1_1bit_7_y));
  mux8_1_1bit mux8_1_1bit_8 (
    .S(B[2:0]), .D_0(1'b0), .D_1(1'b0), .D_2(1'b0), .D_3(1'b0), .D_4(1'b0), .D_5(1'b0), .D_6(1'b0),
    .D_7(1'b0), .Y(mux8_1_1bit_8_y));
  mux2_1 mux2_1_1 (.B(B[3]), .A_0(mux8_1_1bit_1_y), .A_1(mux8_1_1bit_2_y), .Y(Y[15]));
  mux2_1 mux2_1_2 (.B(B[3]), .A_0(mux8_1_1bit_3_y), .A_1(mux8_1_1bit_4_y), .Y(Y[14]));
  mux2_1 mux2_1_3 (.B(B[3]), .A_0(mux8_1_1bit_5_y), .A_1(mux8_1_1bit_6_y), .Y(Y[13]));
  mux2_1 mux2_1_4 (.B(B[3]), .A_0(mux8_1_1bit_7_y), .A_1(mux8_1_1bit_8_y), .Y(Y[12]));
  mux8_1_1bit mux8_1_1bit_9 (
    .S(B[2:0]), .D_0(A[11]), .D_1(A[12]), .D_2(A[13]), .D_3(A[14]), .D_4(A[15]), .D_5(1'b0), .D_6(1'b0),
    .D_7(1'b0), .Y(mux8_1_1bit_9_y));
  mux8_1_1bit mux8_1_1bit_10 (
    .S(B[2:0]), .D_0(1'b0), .D_1(1'b0), .D_2(1'b0), .D_3(1'b0), .D_4(1'b0), .D_5(1'b0), .D_6(1'b0),
    .D_7(1'b0), .Y(mux8_1_1bit_10_y));
  mux8_1_1bit mux8_1_1bit_11 (
    .S(B[2:0]), .D_0(A[10]), .D_1(A[11]), .D_2(A[12]), .D_3(A[13]), .D_4(A[14]), .D_5(A[15]), .D_6(1'b0),
    .D_7(1'b0), .Y(mux8_1_1bit_11_y));
  mux8_1_1bit mux8_1_1bit_12 (
    .S(B[2:0]), .D_0(1'b0), .D_1(1'b0), .D_2(1'b0), .D_3(1'b0), .D_4(1'b0), .D_5(1'b0), .D_6(1'b0),
    .D_7(1'b0), .Y(mux8_1_1bit_12_y));
  mux8_1_1bit mux8_1_1bit_13 (
    .S(B[2:0]), .D_0(A[9]), .D_1(A[10]), .D_2(A[11]), .D_3(A[12]), .D_4(A[13]), .D_5(A[14]), .D_6(A[15]),
    .D_7(1'b0), .Y(mux8_1_1bit_13_y));
  mux8_1_1bit mux8_1_1bit_14 (
    .S(B[2:0]), .D_0(1'b0), .D_1(1'b0), .D_2(1'b0), .D_3(1'b0), .D_4(1'b0), .D_5(1'b0), .D_6(1'b0),
    .D_7(1'b0), .Y(mux8_1_1bit_14_y));
  mux8_1_1bit mux8_1_1bit_15 (
    .S(B[2:0]), .D_0(A[8]), .D_1(A[9]), .D_2(A[10]), .D_3(A[11]), .D_4(A[12]), .D_5(A[13]), .D_6(A[14]),
    .D_7(A[15]), .Y(mux8_1_1bit_15_y));
  mux8_1_1bit mux8_1_1bit_16 (
    .S(B[2:0]), .D_0(1'b0), .D_1(1'b0), .D_2(1'b0), .D_3(1'b0), .D_4(1'b0), .D_5(1'b0), .D_6(1'b0),
    .D_7(1'b0), .Y(mux8_1_1bit_16_y));
  mux2_1 mux2_1_5 (.B(B[3]), .A_0(mux8_1_1bit_9_y), .A_1(mux8_1_1bit_10_y), .Y(Y[11]));
  mux2_1 mux2_1_6 (.B(B[3]), .A_0(mux8_1_1bit_11_y), .A_1(mux8_1_1bit_12_y), .Y(Y[10]));
  mux2_1 mux2_1_7 (.B(B[3]), .A_0(mux8_1_1bit_13_y), .A_1(mux8_1_1bit_14_y), .Y(Y[9]));
  mux2_1 mux2_1_8 (.B(B[3]), .A_0(mux8_1_1bit_15_y), .A_1(mux8_1_1bit_16_y), .Y(Y[8]));
  mux8_1_1bit mux8_1_1bit_17 (
    .S(B[2:0]), .D_0(A[7]), .D_1(A[8]), .D_2(A[9]), .D_3(A[10]), .D_4(A[11]), .D_5(A[12]), .D_6(A[13]),
    .D_7(A[14]), .Y(mux8_1_1bit_17_y));
  mux8_1_1bit mux8_1_1bit_18 (
    .S(B[2:0]), .D_0(A[15]), .D_1(1'b0), .D_2(1'b0), .D_3(1'b0), .D_4(1'b0), .D_5(1'b0), .D_6(1'b0),
    .D_7(1'b0), .Y(mux8_1_1bit_18_y));
  mux8_1_1bit mux8_1_1bit_19 (
    .S(B[2:0]), .D_0(A[6]), .D_1(A[7]), .D_2(A[8]), .D_3(A[9]), .D_4(A[10]), .D_5(A[11]), .D_6(A[12]),
    .D_7(A[13]), .Y(mux8_1_1bit_19_y));
  mux8_1_1bit mux8_1_1bit_20 (
    .S(B[2:0]), .D_0(A[14]), .D_1(A[15]), .D_2(1'b0), .D_3(1'b0), .D_4(1'b0), .D_5(1'b0), .D_6(1'b0),
    .D_7(1'b0), .Y(mux8_1_1bit_20_y));
  mux8_1_1bit mux8_1_1bit_21 (
    .S(B[2:0]), .D_0(A[5]), .D_1(A[6]), .D_2(A[7]), .D_3(A[8]), .D_4(A[9]), .D_5(A[10]), .D_6(A[11]),
    .D_7(A[12]), .Y(mux8_1_1bit_21_y));
  mux8_1_1bit mux8_1_1bit_22 (
    .S(B[2:0]), .D_0(A[13]), .D_1(A[14]), .D_2(A[15]), .D_3(1'b0), .D_4(1'b0), .D_5(1'b0), .D_6(1'b0),
    .D_7(1'b0), .Y(mux8_1_1bit_22_y));
  mux8_1_1bit mux8_1_1bit_23 (
    .S(B[2:0]), .D_0(A[4]), .D_1(A[5]), .D_2(A[6]), .D_3(A[7]), .D_4(A[8]), .D_5(A[9]), .D_6(A[10]),
    .D_7(A[11]), .Y(mux8_1_1bit_23_y));
  mux8_1_1bit mux8_1_1bit_24 (
    .S(B[2:0]), .D_0(A[12]), .D_1(A[13]), .D_2(A[14]), .D_3(A[15]), .D_4(1'b0), .D_5(1'b0), .D_6(1'b0),
    .D_7(1'b0), .Y(mux8_1_1bit_24_y));
  mux2_1 mux2_1_9 (.B(B[3]), .A_0(mux8_1_1bit_17_y), .A_1(mux8_1_1bit_18_y), .Y(Y[7]));
  mux2_1 mux2_1_10 (.B(B[3]), .A_0(mux8_1_1bit_19_y), .A_1(mux8_1_1bit_20_y), .Y(Y[6]));
  mux2_1 mux2_1_11 (.B(B[3]), .A_0(mux8_1_1bit_21_y), .A_1(mux8_1_1bit_22_y), .Y(Y[5]));
  mux2_1 mux2_1_12 (.B(B[3]), .A_0(mux8_1_1bit_23_y), .A_1(mux8_1_1bit_24_y), .Y(Y[4]));
  mux8_1_1bit mux8_1_1bit_25 (
    .S(B[2:0]), .D_0(A[3]), .D_1(A[4]), .D_2(A[5]), .D_3(A[6]), .D_4(A[7]), .D_5(A[8]), .D_6(A[9]),
    .D_7(A[10]), .Y(mux8_1_1bit_25_y));
  mux8_1_1bit mux8_1_1bit_26 (
    .S(B[2:0]), .D_0(A[11]), .D_1(A[12]), .D_2(A[13]), .D_3(A[14]), .D_4(A[15]), .D_5(1'b0), .D_6(1'b0),
    .D_7(1'b0), .Y(mux8_1_1bit_26_y));
  mux8_1_1bit mux8_1_1bit_27 (
    .S(B[2:0]), .D_0(A[2]), .D_1(A[3]), .D_2(A[4]), .D_3(A[5]), .D_4(A[6]), .D_5(A[7]), .D_6(A[8]),
    .D_7(A[9]), .Y(mux8_1_1bit_27_y));
  mux8_1_1bit mux8_1_1bit_28 (
    .S(B[2:0]), .D_0(A[10]), .D_1(A[11]), .D_2(A[12]), .D_3(A[13]), .D_4(A[14]), .D_5(A[15]), .D_6(1'b0),
    .D_7(1'b0), .Y(mux8_1_1bit_28_y));
  mux8_1_1bit mux8_1_1bit_29 (
    .S(B[2:0]), .D_0(A[1]), .D_1(A[2]), .D_2(A[3]), .D_3(A[4]), .D_4(A[5]), .D_5(A[6]), .D_6(A[7]),
    .D_7(A[8]), .Y(mux8_1_1bit_29_y));
  mux8_1_1bit mux8_1_1bit_30 (
    .S(B[2:0]), .D_0(A[9]), .D_1(A[10]), .D_2(A[11]), .D_3(A[12]), .D_4(A[13]), .D_5(A[14]), .D_6(A[15]),
    .D_7(1'b0), .Y(mux8_1_1bit_30_y));
  mux8_1_1bit mux8_1_1bit_31 (
    .S(B[2:0]), .D_0(A[0]), .D_1(A[1]), .D_2(A[2]), .D_3(A[3]), .D_4(A[4]), .D_5(A[5]), .D_6(A[6]),
    .D_7(A[7]), .Y(mux8_1_1bit_31_y));
  mux8_1_1bit mux8_1_1bit_32 (
    .S(B[2:0]), .D_0(A[8]), .D_1(A[9]), .D_2(A[10]), .D_3(A[11]), .D_4(A[12]), .D_5(A[13]), .D_6(A[14]),
    .D_7(A[15]), .Y(mux8_1_1bit_32_y));
  mux2_1 mux2_1_13 (.B(B[3]), .A_0(mux8_1_1bit_25_y), .A_1(mux8_1_1bit_26_y), .Y(Y[3]));
  mux2_1 mux2_1_14 (.B(B[3]), .A_0(mux8_1_1bit_27_y), .A_1(mux8_1_1bit_28_y), .Y(Y[2]));
  mux2_1 mux2_1_15 (.B(B[3]), .A_0(mux8_1_1bit_29_y), .A_1(mux8_1_1bit_30_y), .Y(Y[1]));
  mux2_1 mux2_1_16 (.B(B[3]), .A_0(mux8_1_1bit_31_y), .A_1(mux8_1_1bit_32_y), .Y(Y[0]));

  // Other names for the same wires on the sheet: A_0 = A[0]; A_1 = A[1]; A_2 = A[2]; A_3 = A[3]; A_4 = A[4];
  //   A_5 = A[5]; A_6 = A[6]; A_7 = A[7]; A_8 = A[8]; A_9 = A[9]; A_10 = A[10]; A_11 = A[11]; A_12 = A[12];
  //   A_13 = A[13]; A_14 = A[14]; A_15 = A[15]; B_0_2[2:0] = B[2:0]; B_3 = B[3]; Y_0 = Y[0]; Y_1 = Y[1]; Y_2 = Y[2];
  //   Y_3 = Y[3]; Y_4 = Y[4]; Y_5 = Y[5]; Y_6 = Y[6]; Y_7 = Y[7]; Y_8 = Y[8]; Y_9 = Y[9]; Y_10 = Y[10]; Y_11 = Y[11];
  //   Y_12 = Y[12]; Y_13 = Y[13]; Y_14 = Y[14]; Y_15 = Y[15]

  // Notes on the sheet:
  //   Entradas
  //   Deslocador
  //   Saídas
endmodule
