// Digital circuit mux2-1.dig as structural Verilog
module mux2_1 (
  input  B,
  input  A_0,
  input  A_1,
  output Y
);

  wire and_1_out, and_2_out, not_1_out;

  not not_1 (not_1_out, B);
  and and_1 (and_1_out, A_0, not_1_out);
  and and_2 (and_2_out, A_1, B);
  or or_1 (Y, and_1_out, and_2_out);
endmodule
