// Digital circuit mux8-1_16bits.dig as structural Verilog
module mux8_1_16bits (
  input  [2:0] S,
  input  [15:0] D_0,
  input  [15:0] D_1,
  input  [15:0] D_2,
  input  [15:0] D_3,
  input  [15:0] D_4,
  input  [15:0] D_5,
  input  [15:0] D_6,
  input  [15:0] D_7,
  output [15:0] Y
);

  mux8_1_1bit mux8_1_1bit_1 (
    .S(S), .D_0(D_0[0]), .D_1(D_1[0]), .D_2(D_2[0]), .D_3(D_3[0]), .D_4(D_4[0]), .D_5(D_5[0]), .D_6(D_6[0]),
    .D_7(D_7[0]), .Y(Y[0]));
  mux8_1_1bit mux8_1_1bit_2 (
    .S(S), .D_0(D_0[4]), .D_1(D_1[4]), .D_2(D_2[4]), .D_3(D_3[4]), .D_4(D_4[4]), .D_5(D_5[4]), .D_6(D_6[4]),
    .D_7(D_7[4]), .Y(Y[4]));
  mux8_1_1bit mux8_1_1bit_3 (
    .S(S), .D_0(D_0[8]), .D_1(D_1[8]), .D_2(D_2[8]), .D_3(D_3[8]), .D_4(D_4[8]), .D_5(D_5[8]), .D_6(D_6[8]),
    .D_7(D_7[8]), .Y(Y[8]));
  mux8_1_1bit mux8_1_1bit_4 (
    .S(S), .D_0(D_0[12]), .D_1(D_1[12]), .D_2(D_2[12]), .D_3(D_3[12]), .D_4(D_4[12]), .D_5(D_5[12]),
    .D_6(D_6[12]), .D_7(D_7[12]), .Y(Y[12]));
  mux8_1_1bit mux8_1_1bit_5 (
    .S(S), .D_0(D_0[1]), .D_1(D_1[1]), .D_2(D_2[1]), .D_3(D_3[1]), .D_4(D_4[1]), .D_5(D_5[1]), .D_6(D_6[1]),
    .D_7(D_7[1]), .Y(Y[1]));
  mux8_1_1bit mux8_1_1bit_6 (
    .S(S), .D_0(D_0[5]), .D_1(D_1[5]), .D_2(D_2[5]), .D_3(D_3[5]), .D_4(D_4[5]), .D_5(D_5[5]), .D_6(D_6[5]),
    .D_7(D_7[5]), .Y(Y[5]));
  mux8_1_1bit mux8_1_1bit_7 (
    .S(S), .D_0(D_0[9]), .D_1(D_1[9]), .D_2(D_2[9]), .D_3(D_3[9]), .D_4(D_4[9]), .D_5(D_5[9]), .D_6(D_6[9]),
    .D_7(D_7[9]), .Y(Y[9]));
  mux8_1_1bit mux8_1_1bit_8 (
    .S(S), .D_0(D_0[13]), .D_1(D_1[13]), .D_2(D_2[13]), .D_3(D_3[13]), .D_4(D_4[13]), .D_5(D_5[13]),
    .D_6(D_6[13]), .D_7(D_7[13]), .Y(Y[13]));
  mux8_1_1bit mux8_1_1bit_9 (
    .S(S), .D_0(D_0[2]), .D_1(D_1[2]), .D_2(D_2[2]), .D_3(D_3[2]), .D_4(D_4[2]), .D_5(D_5[2]), .D_6(D_6[2]),
    .D_7(D_7[2]), .Y(Y[2]));
  mux8_1_1bit mux8_1_1bit_10 (
    .S(S), .D_0(D_0[6]), .D_1(D_1[6]), .D_2(D_2[6]), .D_3(D_3[6]), .D_4(D_4[6]), .D_5(D_5[6]), .D_6(D_6[6]),
    .D_7(D_7[6]), .Y(Y[6]));
  mux8_1_1bit mux8_1_1bit_11 (
    .S(S), .D_0(D_0[10]), .D_1(D_1[10]), .D_2(D_2[10]), .D_3(D_3[10]), .D_4(D_4[10]), .D_5(D_5[10]),
    .D_6(D_6[10]), .D_7(D_7[10]), .Y(Y[10]));
  mux8_1_1bit mux8_1_1bit_12 (
    .S(S), .D_0(D_0[14]), .D_1(D_1[14]), .D_2(D_2[14]), .D_3(D_3[14]), .D_4(D_4[14]), .D_5(D_5[14]),
    .D_6(D_6[14]), .D_7(D_7[14]), .Y(Y[14]));
  mux8_1_1bit mux8_1_1bit_13 (
    .S(S), .D_0(D_0[3]), .D_1(D_1[3]), .D_2(D_2[3]), .D_3(D_3[3]), .D_4(D_4[3]), .D_5(D_5[3]), .D_6(D_6[3]),
    .D_7(D_7[3]), .Y(Y[3]));
  mux8_1_1bit mux8_1_1bit_14 (
    .S(S), .D_0(D_0[7]), .D_1(D_1[7]), .D_2(D_2[7]), .D_3(D_3[7]), .D_4(D_4[7]), .D_5(D_5[7]), .D_6(D_6[7]),
    .D_7(D_7[7]), .Y(Y[7]));
  mux8_1_1bit mux8_1_1bit_15 (
    .S(S), .D_0(D_0[11]), .D_1(D_1[11]), .D_2(D_2[11]), .D_3(D_3[11]), .D_4(D_4[11]), .D_5(D_5[11]),
    .D_6(D_6[11]), .D_7(D_7[11]), .Y(Y[11]));
  mux8_1_1bit mux8_1_1bit_16 (
    .S(S), .D_0(D_0[15]), .D_1(D_1[15]), .D_2(D_2[15]), .D_3(D_3[15]), .D_4(D_4[15]), .D_5(D_5[15]),
    .D_6(D_6[15]), .D_7(D_7[15]), .Y(Y[15]));

  // Other names for the same wires on the sheet: D0_0 = D_0[0]; D0_1 = D_0[1]; D0_2 = D_0[2]; D0_3 = D_0[3];
  //   D0_4 = D_0[4]; D0_5 = D_0[5]; D0_6 = D_0[6]; D0_7 = D_0[7]; D0_8 = D_0[8]; D0_9 = D_0[9]; D0_10 = D_0[10];
  //   D0_11 = D_0[11]; D0_12 = D_0[12]; D0_13 = D_0[13]; D0_14 = D_0[14]; D0_15 = D_0[15]; D1_0 = D_1[0];
  //   D1_1 = D_1[1]; D1_2 = D_1[2]; D1_3 = D_1[3]; D1_4 = D_1[4]; D1_5 = D_1[5]; D1_6 = D_1[6]; D1_7 = D_1[7];
  //   D1_8 = D_1[8]; D1_9 = D_1[9]; D1_10 = D_1[10]; D1_11 = D_1[11]; D1_12 = D_1[12]; D1_13 = D_1[13];
  //   D1_14 = D_1[14]; D1_15 = D_1[15]; D2_0 = D_2[0]; D2_1 = D_2[1]; D2_2 = D_2[2]; D2_3 = D_2[3]; D2_4 = D_2[4];
  //   D2_5 = D_2[5]; D2_6 = D_2[6]; D2_7 = D_2[7]; D2_8 = D_2[8]; D2_9 = D_2[9]; D2_10 = D_2[10]; D2_11 = D_2[11];
  //   D2_12 = D_2[12]; D2_13 = D_2[13]; D2_14 = D_2[14]; D2_15 = D_2[15]; D3_0 = D_3[0]; D3_1 = D_3[1]; D3_2 = D_3[2];
  //   D3_3 = D_3[3]; D3_4 = D_3[4]; D3_5 = D_3[5]; D3_6 = D_3[6]; D3_7 = D_3[7]; D3_8 = D_3[8]; D3_9 = D_3[9];
  //   D3_10 = D_3[10]; D3_11 = D_3[11]; D3_12 = D_3[12]; D3_13 = D_3[13]; D3_14 = D_3[14]; D3_15 = D_3[15];
  //   D4_0 = D_4[0]; D4_1 = D_4[1]; D4_2 = D_4[2]; D4_3 = D_4[3]; D4_4 = D_4[4]; D4_5 = D_4[5]; D4_6 = D_4[6];
  //   D4_7 = D_4[7]; D4_8 = D_4[8]; D4_9 = D_4[9]; D4_10 = D_4[10]; D4_11 = D_4[11]; D4_12 = D_4[12]; D4_13 = D_4[13];
  //   D4_14 = D_4[14]; D4_15 = D_4[15]; D5_0 = D_5[0]; D5_1 = D_5[1]; D5_2 = D_5[2]; D5_3 = D_5[3]; D5_4 = D_5[4];
  //   D5_5 = D_5[5]; D5_6 = D_5[6]; D5_7 = D_5[7]; D5_8 = D_5[8]; D5_9 = D_5[9]; D5_10 = D_5[10]; D5_11 = D_5[11];
  //   D5_12 = D_5[12]; D5_13 = D_5[13]; D5_14 = D_5[14]; D5_15 = D_5[15]; D6_0 = D_6[0]; D6_1 = D_6[1]; D6_2 = D_6[2];
  //   D6_3 = D_6[3]; D6_4 = D_6[4]; D6_5 = D_6[5]; D6_6 = D_6[6]; D6_7 = D_6[7]; D6_8 = D_6[8]; D6_9 = D_6[9];
  //   D6_10 = D_6[10]; D6_11 = D_6[11]; D6_12 = D_6[12]; D6_13 = D_6[13]; D6_14 = D_6[14]; D6_15 = D_6[15];
  //   D7_0 = D_7[0]; D7_1 = D_7[1]; D7_2 = D_7[2]; D7_3 = D_7[3]; D7_4 = D_7[4]; D7_5 = D_7[5]; D7_6 = D_7[6];
  //   D7_7 = D_7[7]; D7_8 = D_7[8]; D7_9 = D_7[9]; D7_10 = D_7[10]; D7_11 = D_7[11]; D7_12 = D_7[12]; D7_13 = D_7[13];
  //   D7_14 = D_7[14]; D7_15 = D_7[15]; Y_0 = Y[0]; Y_1 = Y[1]; Y_2 = Y[2]; Y_3 = Y[3]; Y_4 = Y[4]; Y_5 = Y[5];
  //   Y_6 = Y[6]; Y_7 = Y[7]; Y_8 = Y[8]; Y_9 = Y[9]; Y_10 = Y[10]; Y_11 = Y[11]; Y_12 = Y[12]; Y_13 = Y[13];
  //   Y_14 = Y[14]; Y_15 = Y[15]

  // Notes on the sheet:
  //   Entradas
  //   MUX 8:1
  //   Saídas
endmodule
