// Digital circuit mux8-1_1bit.dig as structural Verilog
module mux8_1_1bit (
  input  [2:0] S,
  input  D_0,
  input  D_1,
  input  D_2,
  input  D_3,
  input  D_4,
  input  D_5,
  input  D_6,
  input  D_7,
  output Y
);

  wire and_1_out, and_2_out, and_3_out, and_4_out, and_5_out, and_6_out, and_7_out, and_8_out, not_1_out,
       not_2_out, not_3_out, or_1_out, or_2_out;

  not not_1 (not_1_out, S[2]);
  not not_2 (not_2_out, S[1]);
  not not_3 (not_3_out, S[0]);
  and and_1 (and_1_out, D_0, not_1_out, not_2_out, not_3_out);
  and and_2 (and_2_out, D_1, not_1_out, not_2_out, S[0]);
  and and_3 (and_3_out, D_2, not_1_out, S[1], not_3_out);
  and and_4 (and_4_out, D_3, not_1_out, S[1], S[0]);
  and and_5 (and_5_out, D_4, S[2], not_2_out, not_3_out);
  and and_6 (and_6_out, D_5, S[2], not_2_out, S[0]);
  and and_7 (and_7_out, D_6, S[2], S[1], not_3_out);
  and and_8 (and_8_out, D_7, S[2], S[1], S[0]);
  or or_1 (or_1_out, and_1_out, and_2_out, and_3_out, and_4_out);
  or or_2 (or_2_out, and_5_out, and_6_out, and_7_out, and_8_out);
  or or_3 (Y, or_1_out, or_2_out);

  // Other names for the same wires on the sheet: S_0 = S[0]; S_1 = S[1]; S_2 = S[2]
endmodule
