// Digital circuit somador_16bits.dig as structural Verilog
module somador_16bits (
  input  [15:0] A,
  input  [15:0] B,
  input  Ci,
  output [15:0] S,
  output Ov
);

  wire somador_1bit_1_co, somador_1bit_2_co, somador_1bit_3_co, somador_1bit_4_co, somador_1bit_5_co,
       somador_1bit_6_co, somador_1bit_7_co, somador_1bit_8_co, somador_1bit_9_co, somador_1bit_10_co,
       somador_1bit_11_co, somador_1bit_12_co, somador_1bit_13_co, somador_1bit_14_co, somador_1bit_15_co,
       somador_1bit_16_co;

  xor xor_1 (Ov, somador_1bit_4_co, somador_1bit_8_co);
  somador_1bit somador_1bit_1 (.A(A[0]), .B(B[0]), .Ci(Ci), .S(S[0]), .Co(somador_1bit_1_co));
  somador_1bit somador_1bit_2 (.A(A[8]), .B(B[8]), .Ci(somador_1bit_3_co), .S(S[8]), .Co(somador_1bit_2_co));
  somador_1bit somador_1bit_3 (.A(A[7]), .B(B[7]), .Ci(somador_1bit_6_co), .S(S[7]), .Co(somador_1bit_3_co));
  somador_1bit somador_1bit_4 (.A(A[15]), .B(B[15]), .Ci(somador_1bit_8_co), .S(S[15]), .Co(somador_1bit_4_co));
  somador_1bit somador_1bit_5 (.A(A[1]), .B(B[1]), .Ci(somador_1bit_1_co), .S(S[1]), .Co(somador_1bit_5_co));
  somador_1bit somador_1bit_6 (.A(A[6]), .B(B[6]), .Ci(somador_1bit_11_co), .S(S[6]), .Co(somador_1bit_6_co));
  somador_1bit somador_1bit_7 (.A(A[9]), .B(B[9]), .Ci(somador_1bit_2_co), .S(S[9]), .Co(somador_1bit_7_co));
  somador_1bit somador_1bit_8 (.A(A[14]), .B(B[14]), .Ci(somador_1bit_12_co), .S(S[14]), .Co(somador_1bit_8_co));
  somador_1bit somador_1bit_9 (.A(A[2]), .B(B[2]), .Ci(somador_1bit_5_co), .S(S[2]), .Co(somador_1bit_9_co));
  somador_1bit somador_1bit_10 (.A(A[10]), .B(B[10]), .Ci(somador_1bit_7_co), .S(S[10]), .Co(somador_1bit_10_co));
  somador_1bit somador_1bit_11 (.A(A[5]), .B(B[5]), .Ci(somador_1bit_15_co), .S(S[5]), .Co(somador_1bit_11_co));
  somador_1bit somador_1bit_12 (.A(A[13]), .B(B[13]), .Ci(somador_1bit_16_co), .S(S[13]), .Co(somador_1bit_12_co));
  somador_1bit somador_1bit_13 (.A(A[3]), .B(B[3]), .Ci(somador_1bit_9_co), .S(S[3]), .Co(somador_1bit_13_co));
  somador_1bit somador_1bit_14 (.A(A[11]), .B(B[11]), .Ci(somador_1bit_10_co), .S(S[11]), .Co(somador_1bit_14_co));
  somador_1bit somador_1bit_15 (.A(A[4]), .B(B[4]), .Ci(somador_1bit_13_co), .S(S[4]), .Co(somador_1bit_15_co));
  somador_1bit somador_1bit_16 (.A(A[12]), .B(B[12]), .Ci(somador_1bit_14_co), .S(S[12]), .Co(somador_1bit_16_co));

  // Other names for the same wires on the sheet: A_0 = A[0]; A_1 = A[1]; A_2 = A[2]; A_3 = A[3]; A_4 = A[4];
  //   A_5 = A[5]; A_6 = A[6]; A_7 = A[7]; A_8 = A[8]; A_9 = A[9]; A_10 = A[10]; A_11 = A[11]; A_12 = A[12];
  //   A_13 = A[13]; A_14 = A[14]; A_15 = A[15]; B_0 = B[0]; B_1 = B[1]; B_2 = B[2]; B_3 = B[3]; B_4 = B[4];
  //   B_5 = B[5]; B_6 = B[6]; B_7 = B[7]; B_8 = B[8]; B_9 = B[9]; B_10 = B[10]; B_11 = B[11]; B_12 = B[12];
  //   B_13 = B[13]; B_14 = B[14]; B_15 = B[15]; S_0 = S[0]; S_1 = S[1]; S_2 = S[2]; S_3 = S[3]; S_4 = S[4];
  //   S_5 = S[5]; S_6 = S[6]; S_7 = S[7]; S_8 = S[8]; S_9 = S[9]; S_10 = S[10]; S_11 = S[11]; S_12 = S[12];
  //   S_13 = S[13]; S_14 = S[14]; S_15 = S[15]

  // Notes on the sheet:
  //   Entradas
  //   Somador
  //   Saídas
endmodule
