// Digital circuit somador_1bit.dig as structural Verilog
module somador_1bit (
  input  A,
  input  B,
  input  Ci,
  output S,
  output Co
);

  wire and_1_out, and_2_out, or_1_out;

  xor xor_1 (S, Ci, A, B);
  or or_1 (or_1_out, A, B);
  and and_1 (and_1_out, A, B);
  and and_2 (and_2_out, or_1_out, Ci);
  or or_2 (Co, and_1_out, and_2_out);
endmodule
