// Digital circuit ula.dig as structural Verilog
module ula (
  input  [15:0] A,
  input  [15:0] B,
  input  [2:0] F,
  output [15:0] R,
  output S_0,
  output S_1,
  output S_2
);

  wire and_1_out, and_2_out, and_3_out, and_4_out, D4_ov, D5_ov, D6_ov, D7_ov;
  wire [15:0] A___1_s, A___B_s, A__gt__gt__B_3_0_y, A__lt__lt__B_3_0_y, A__plus__1_s, A__plus__B_s, A_B_y,
       A_y, not_1_out, not_2_out, not_3_out;

  assign not_1_out = ~B;  // Not not_1, 16 bits wide
  assign not_2_out = ~16'h1;  // Not not_2, 16 bits wide
  deslocador_esquerda A__lt__lt__B_3_0 (.A(A), .B(B), .Y(A__lt__lt__B_3_0_y));
  deslocador_direita A__gt__gt__B_3_0 (.A(A), .B(B), .Y(A__gt__gt__B_3_0_y));
  \xor  A_B (.A(A), .B(B), .Y(A_B_y));
  inversor u_A (.A(A), .Y(A_y));
  somador_16bits A__plus__B (.A(A), .B(B), .Ci(1'b0), .S(A__plus__B_s), .Ov(D4_ov));
  somador_16bits A___B (.A(A), .B(not_1_out), .Ci(1'b1), .S(A___B_s), .Ov(D5_ov));
  somador_16bits A__plus__1 (.A(A), .B(16'h1), .Ci(1'b0), .S(A__plus__1_s), .Ov(D6_ov));
  somador_16bits A___1 (.A(A), .B(not_2_out), .Ci(1'b1), .S(A___1_s), .Ov(D7_ov));
  mux8_1_16bits mux8_1_16bits_1 (
    .S(F), .D_0(A__lt__lt__B_3_0_y), .D_1(A__gt__gt__B_3_0_y), .D_2(A_B_y), .D_3(A_y), .D_4(A__plus__B_s),
    .D_5(A___B_s), .D_6(A__plus__1_s), .D_7(A___1_s), .Y(R));
  assign not_3_out = ~R;  // Not not_3, 16 bits wide
  and and_1 (and_1_out, not_3_out[0], not_3_out[1], not_3_out[2], not_3_out[3]);
  and and_2 (and_2_out, not_3_out[4], not_3_out[5], not_3_out[6], not_3_out[7]);
  and and_3 (and_3_out, not_3_out[8], not_3_out[9], not_3_out[10], not_3_out[11]);
  and and_4 (and_4_out, not_3_out[12], not_3_out[13], not_3_out[14], not_3_out[15]);
  not not_4 (S_2, not_3_out[15]);
  mux8_1_1bit mux8_1_1bit_1 (
    .S(F), .D_0(1'b0), .D_1(1'b0), .D_2(1'b0), .D_3(1'b0), .D_4(D4_ov), .D_5(D5_ov), .D_6(D6_ov),
    .D_7(D7_ov), .Y(S_1));
  and and_5 (S_0, and_1_out, and_2_out, and_3_out, and_4_out);

  // Notes on the sheet:
  //   Testes
  //   Túneis
  //   Operações
  //   Saídas
endmodule

/* Test case A << B_{3:0}:
A      B      F R      S_0  S_1 S_2
0      0      0 0      1    0   0
0      1      0 0      1    0   0

0xFFFF 1      0 0xFFFE 0    0   1
0xFFFF 6      0 0xFFC0 0    0   1
0xFFFF 0x000F 0 0x8000 0    0   1
0xFFFF 0xFFFF 0 0x8000 0    0   1

0xAAAA 2      0 0xAAA8 0    0   1     
*/

/* Test case A >> B_{3:0}:
A      B      F R      S_0  S_1 S_2
0      0      1 0      1    0   0
0      1      1 0      1    0   0

0xFFFF 1      1 0x7FFF 0    0   0
0xFFFF 6      1 0x3FF  0    0   0
0xFFFF 0x000F 1 1      0    0   0
0xFFFF 0xFFFF 1 1      0    0   0

0xAAAA 2      1 0x2AAA 0    0   0     
*/

/* Test case A⊕B:
A      B      F R      S_0  S_1 S_2
0      0      2 0      1    0   0

0xFFFF 0      2 0xFFFF 0    0   1
0xFFFF 0xFFF0 2 0x000F 0    0   0
0xFFFF 0xFFFF 2 0      1    0   0

0x5555 0xAAAA 2 0xFFFF 0    0   1
0xAAAA 0x5555 2 0xFFFF 0    0   1
*/

/* Test case !A:
A      F R      S_0  S_1 S_2
0      3 0xFFFF 0    0   1
0xFFFF 3 0      1    0   0
0x5555 3 0xAAAA 0    0   1
0xAAAA 3 0x5555 0    0   0
*/

/* Test case A + B:
A      B      F R      S_0  S_1 S_2
0      0      4 0      1    0   0
0xFFFF 2      4 1      0    0   0
0x5555 0x5555 4 0xAAAA 0    1   1
0xAAAA 0xAAAA 4 0x5554 0    1   0
*/

/* Test case A - B:
A      B      F R      S_0  S_1 S_2
0      0      5 0      1    0   0
0xFFFF 2      5 0xFFFD 0    0   1
0x5555 0x5555 5 0      1    0   0
0x5555 0xAAAB 5 0xAAAA 0    1   1
0xAAAA 0xAAAA 5 0      1    0   0
*/

/* Test case A + 1:
A      F R      S_0  S_1 S_2
0      6 1      0    0   0
0xFFFF 6 0      1    0   0
0x5555 6 0x5556 0    0   0
0xAAAA 6 0xAAAB 0    0   1
*/

/* Test case A - 1:
A      F R      S_0  S_1 S_2
0      7 0xFFFF 0    0   1
0xFFFF 7 0xFFFE 0    0   1
0x5555 7 0x5554 0    0   0
0xAAAA 7 0XAAA9 0    0   1
*/
