// Digital circuit ula_principal.dig as structural Verilog
module ula_principal (
  input  [15:0] A,
  input  [2:0] F,
  input  [15:0] B,
  output [15:0] R,
  output S_0__ZERO,
  output S_1__OVFL,
  output S_2__NEG
);

  ula ula_1 (.A(A), .B(B), .F(F), .R(R), .S_0(S_0__ZERO), .S_1(S_1__OVFL), .S_2(S_2__NEG));

  // Notes on the sheet:
  //   A: Entrada que representa um dos elementos da operação lógico-aritmética.
  //   F: Entrada que define a operação a ser realizada.
  //   B: Entrada que representa um dos elementos da operação lógico-aritmética.
  //   R: Resultado da operação.
  //   S_0__ZERO: Indica se a saída R é igual a zero (1) ou não (0)
  //   S_1__OVFL: Indica se houve overflow na operação aritmética (1) ou não (0).
  //   S_2__NEG: Indica se a saída R é negativa  (1) ou não (0).
endmodule
