// Logisim project circuito.circ as structural Verilog: 7 circuits, main circuit main
module main (
);

  wire and_1_out, B, clock_1_out, FFA0_q0, FFA1_q0, FFA2_q0, FFA3_q0, latchsr_1_q0, not_1_out, not_2_out,
       not_3_out, not_4_out, not_5_out, or_1_out, P, proximo_estado_1_c0, proximo_estado_1_c1,
       proximo_estado_1_c2, proximo_estado_1_c3, Reset, S1G, S1R, S1Y, S2G, S2R, S2Y, S3G, S3R, S3Y,
       saida_1_s1_0, saida_1_s1_1, saida_1_s2_0, saida_1_s2_1, saida_1_s3_0, saida_1_s3_1;

  Clock clock_1 (.out(clock_1_out));
  FlipFlopD_reset FFA0 (.D(proximo_estado_1_c0), .R(Reset), .Clk(clock_1_out), .Q0(FFA0_q0));  // open: Q1
  FlipFlopD_reset FFA1 (.D(proximo_estado_1_c1), .R(Reset), .Clk(clock_1_out), .Q0(FFA1_q0));  // open: Q1
  FlipFlopD_reset FFA2 (.D(proximo_estado_1_c2), .R(Reset), .Clk(clock_1_out), .Q0(FFA2_q0));  // open: Q1
  FlipFlopD_reset FFA3 (.D(proximo_estado_1_c3), .R(Reset), .Clk(clock_1_out), .Q0(FFA3_q0));  // open: Q1
  not not_1 (not_1_out, P);
  and and_1 (and_1_out, B, not_1_out);
  or or_1 (or_1_out, P, Reset);
  Saida saida_1 (
    .A0(FFA0_q0), .A1(FFA1_q0), .A2(FFA2_q0), .A3(FFA3_q0), .S1_1(saida_1_s1_1), .S1_0(saida_1_s1_0),
    .S2_1(saida_1_s2_1), .S2_0(saida_1_s2_0), .S3_1(saida_1_s3_1), .S3_0(saida_1_s3_0), .P(P));
  LatchSR latchsr_1 (.S(and_1_out), .E(1'b1), .R(or_1_out), .Q0(latchsr_1_q0));  // open: Q1
  Decoder_semaforos S1 (.S1(saida_1_s1_1), .S0(saida_1_s1_0), .D0(S1R), .D1(S1Y), .D2(S1G));
  Decoder_semaforos S2 (.S1(saida_1_s2_1), .S0(saida_1_s2_0), .D0(S2R), .D1(S2Y), .D2(S2G));
  Decoder_semaforos S3 (.S1(saida_1_s3_1), .S0(saida_1_s3_0), .D0(S3R), .D1(S3Y), .D2(S3G));
  Proximo_estado proximo_estado_1 (
    .B(latchsr_1_q0), .A0(FFA0_q0), .A1(FFA1_q0), .A2(FFA2_q0), .A3(FFA3_q0), .C0(proximo_estado_1_c0),
    .C1(proximo_estado_1_c1), .C2(proximo_estado_1_c2), .C3(proximo_estado_1_c3));
  Button button_1 (.out(Reset));
  Button button_2 (.out(B));
  not not_2 (not_2_out, P);
  LED led_1 (.in(not_2_out));
  LED led_2 (.in(P));
  LED led_3 (.in(S1R));
  LED led_4 (.in(S1Y));
  LED led_5 (.in(S1G));
  not not_3 (not_3_out, P);
  LED led_6 (.in(not_3_out));
  LED led_7 (.in(P));
  LED led_8 (.in(S2R));
  LED led_9 (.in(S2Y));
  LED led_10 (.in(S2G));
  not not_4 (not_4_out, P);
  LED led_11 (.in(not_4_out));
  LED led_12 (.in(P));
  LED led_13 (.in(S3G));
  LED led_14 (.in(S3Y));
  LED led_15 (.in(S3R));
  not not_5 (not_5_out, P);
  LED led_16 (.in(not_5_out));
  LED led_17 (.in(P));

  // Notes on the sheet:
  //   Botões
  //   S1
  //   S3
  //   S2
endmodule

module LatchSR (
  input  S,
  input  E,
  input  R,
  output Q0,
  output Q1
);

  wire nand_1_out, nand_2_out;

  nand nand_1 (nand_1_out, S, E);
  nand nand_2 (nand_2_out, E, R);
  nand nand_3 (Q0, nand_1_out, Q1);
  nand nand_4 (Q1, Q0, nand_2_out);
endmodule

module Decoder_semaforos (
  input  S1,
  input  S0,
  output D0,
  output D1,
  output D2
);

  wire not_1_out, not_2_out;

  not not_1 (not_1_out, S1);
  not not_2 (not_2_out, S0);
  and and_1 (D0, not_1_out, not_2_out);

  assign D1 = S0;
  assign D2 = S1;
endmodule

module Proximo_estado (
  input  B,
  input  A0,
  input  A1,
  input  A2,
  input  A3,
  output C0,
  output C1,
  output C2,
  output C3
);

  wire and_1_out, and_2_out, and_3_out, and_4_out, and_5_out, and_6_out, and_7_out, and_8_out, and_9_out,
       not_1_out, not_2_out, not_3_out, not_4_out, not_5_out;

  not not_1 (not_1_out, B);
  not not_2 (not_2_out, A0);
  not not_3 (not_3_out, A1);
  not not_4 (not_4_out, A2);
  not not_5 (not_5_out, A3);
  and and_1 (and_1_out, not_5_out, not_3_out, not_2_out);
  and and_2 (and_2_out, not_5_out, not_4_out, A1, not_2_out);
  or or_1 (C0, and_1_out, and_2_out, and_3_out);
  and and_3 (and_3_out, B, not_5_out, not_4_out, A1);
  and and_4 (and_4_out, not_5_out, not_4_out, not_3_out, A0);
  and and_5 (and_5_out, B, not_5_out, not_4_out, A1);
  or or_2 (C1, and_4_out, and_5_out, and_6_out);
  and and_6 (and_6_out, not_1_out, not_5_out, A1, not_2_out);
  and and_7 (and_7_out, not_5_out, A2, not_3_out, not_2_out);
  and and_8 (and_8_out, B, not_5_out, not_4_out, A0);
  or or_3 (C2, and_7_out, and_8_out, and_9_out);
  and and_9 (and_9_out, not_1_out, not_5_out, A1, A0);
  and and_10 (C3, B, not_5_out, A2, not_3_out, A0);
endmodule

module Saida (
  input  A0,
  input  A1,
  input  A2,
  input  A3,
  output S1_1,
  output S1_0,
  output S2_1,
  output S2_0,
  output S3_1,
  output S3_0,
  output P
);

  wire and_7_out, and_8_out, not_1_out, not_2_out, not_3_out, not_4_out;

  not not_1 (not_1_out, A0);
  not not_2 (not_2_out, A1);
  not not_3 (not_3_out, A2);
  not not_4 (not_4_out, A3);
  and and_1 (S1_1, not_4_out, not_3_out, A1, not_1_out);
  and and_2 (S1_0, not_4_out, not_3_out, A1, A0);
  and and_3 (S2_1, not_4_out, A2, not_2_out, not_1_out);
  and and_4 (S2_0, not_4_out, A2, not_2_out, A0);
  and and_5 (S3_1, not_4_out, not_3_out, not_2_out, not_1_out);
  and and_6 (S3_0, not_4_out, not_3_out, not_2_out, A0);
  and and_7 (and_7_out, not_4_out, A2, A1);
  or or_1 (P, and_7_out, and_8_out);
  and and_8 (and_8_out, A3, not_3_out, not_2_out, not_1_out);
endmodule

module Mux_2x1 (
  input  D0,
  input  D1,
  input  S,
  output Y
);

  wire not_1_out, not_2_out;

  not not_1 (not_1_out, D1);
  not not_2 (not_2_out, S);
  and and_1 (Y, D0, not_1_out, not_2_out);
endmodule

module FlipFlopD_reset (
  input  D,
  input  R,
  input  Clk,
  output Q0,
  output Q1
);

  wire latchsr_1_q0, latchsr_1_q1, mux_2x1_1_y, not_1_out, not_2_out;

  Mux_2x1 mux_2x1_1 (.D0(D), .D1(1'b0), .S(R), .Y(mux_2x1_1_y));
  not not_1 (not_1_out, mux_2x1_1_y);
  not not_2 (not_2_out, Clk);
  LatchSR latchsr_1 (.S(mux_2x1_1_y), .E(not_2_out), .R(not_1_out), .Q0(latchsr_1_q0), .Q1(latchsr_1_q1));
  LatchSR latchsr_2 (.S(latchsr_1_q0), .E(Clk), .R(latchsr_1_q1), .Q0(Q0), .Q1(Q1));
endmodule
